# Fritzing sketch throttle-controller (saved by Fritzing 0.9.2b)

parts:
  Pro_Micro1 = Pro Micro
  S1 = Round Pushbutton
  U1 = POT [package=pot_mammoth]
  BAT1 = BC9VPC [package=bc9vpc]
  M1 = DC Motor

nets:
  N1: Pro_Micro1.GND#3, BAT1.V-
  N2: Pro_Micro1.GND#4, S1.leg1
  N3: Pro_Micro1.D2, S1.leg0
  N4: Pro_Micro1.D16/MOSI, M1.pin_1
  N5: Pro_Micro1.D20/A2, U1.A
  N6: Pro_Micro1.VCC, U1.S
  N7: Pro_Micro1.GND#23, U1.E, M1.pin_2
  N8: Pro_Micro1.RAW, BAT1.V+

custom parts:
  Pro Micro: The SparkFun Pro Micro is a complete USB-based microcontoller development system, in a very small footprint, capable of implementing many types of projects. All programming can be done via the USB port.
